# Fritzing sketch bench (saved by Fritzing 1.0.6)
breadboards: 1

parts:
  Pro_Micro = SparkFun Pro Micro
  PS/2_socket = PS/2 socket

nets:
  N1: Pro_Micro.GND, PS/2_socket.3_GND
  N2: Pro_Micro.D3, PS/2_socket.1_DATA
  N3: Pro_Micro.D2, PS/2_socket.5_CLOCK

notes:
  Прошивка: flash. Питание только по USB.
  PS/2 гнездо на ПК, вид с лица, ключ сверху:
  1 DATA, 3 GND, 5 CLOCK; 4 (+5 V) не подключать.
  Перед включением прозвонить при выключенном ПК:
  D2 → гнездо 5, D3 → гнездо 1, GND → гнездо 3,
  каждый провод звенит только на своём пине.
  Звенит на 6 или 2 — распиновка зеркальная.

custom parts:
  SparkFun Pro Micro: This tiny little board does all of the neat-o Arduino tricks that you’re familiar with: 4 channels of 10-bit ADC, 5 PWM pins, 12 DIOs as well as hardware serial connections Rx and Tx. Running at 16MHz and 5V, this board will remind you a lot of your other favorite Arduino-compatible boards but this little guy can go just about anywhere. There is a voltage regulator on board so it can accept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
  PS/2 socket: PS/2 keyboard socket (mini-DIN-6, female), face view: 1 DATA, 3 GND, 4 +5V, 5 CLOCK, 2/6 NC.
